// Digital circuit Block2.dig as structural Verilog
module Block2 (
  input  [47:0] Plain,
  input  [35:0] Key,
  output [47:0] Enc
);

  wire [23:0] and_1_out, and_2_out;

  assign and_1_out = Plain[23:0] & Key[23:0];  // And and_1, 24 bits wide
  assign Enc[23:0] = and_1_out ^ Plain[47:24];  // XOr xor_1, 24 bits wide
  assign and_2_out = Enc[23:0] & Key[35:12];  // And and_2, 24 bits wide
  assign Enc[47:24] = and_2_out ^ Plain[23:0];  // XOr xor_2, 24 bits wide

  // Other names for the same wires on the sheet: Key1[23:0] = Key[23:0]; Key2[23:0] = Key[35:12]
endmodule
