// Digital circuit Block3.dig as structural Verilog
module Block3 (
  input  [63:0] Plain,
  input  Clock,
  output [63:0] Enc
);

  wire delay_1_out, delay_2_out, rs_ff_as_1_nq;
  wire [63:0] driver_1_out, xor_1_out;
  wire [63:1] register_1_q;
  wire [63:63] register_1_q_2;

  RS_FF_AS rs_ff_as_1 (.S(Clock), .R(1'b0), .nQ(rs_ff_as_1_nq));  // open: Q
  assign driver_1_out = rs_ff_as_1_nq ? Plain : 64'bz;  // Driver driver_1
  assign driver_1_out = Clock ? {register_1_q, 1'b0} : 64'bz;  // Driver driver_2
  Delay delay_1 (.in(Clock), .out(delay_1_out));
  Register #(.Bits(64)) register_1 (
    .D(driver_1_out), .C(delay_1_out), .en(Clock), .Q({register_1_q_2[63], register_1_q}));
  assign xor_1_out = Enc ^ {register_1_q_2[63], register_1_q};  // XOr xor_1, 64 bits wide
  Register #(.Bits(64)) register_2 (.D(xor_1_out), .C(delay_2_out), .en(Clock), .Q(Enc));
  Delay delay_2 (.in(Clock), .out(delay_2_out));

  // Notes on the sheet:
  //   Clock: Hz: 100
endmodule
