// Digital circuit Block2.dig as structural Verilog
module Block2 (
  input  [47:0] Plain,
  input  [47:0] Key,
  output [47:0] Enc
);

  wire [23:0] xnor_1_out, xnor_2_out, xnor_3_out, xor_1_out;

  assign xnor_1_out = ~(Plain[23:0] ^ Key[23:0]);  // XNOr xnor_1, 24 bits wide
  assign xor_1_out = xnor_1_out ^ Plain[47:24];  // XOr xor_1, 24 bits wide
  assign xnor_2_out = ~(xor_1_out ^ Key[35:12]);  // XNOr xnor_2, 24 bits wide
  assign Enc[23:0] = xnor_2_out ^ Plain[23:0];  // XOr xor_2, 24 bits wide
  assign xnor_3_out = ~(Enc[23:0] ^ Key[47:24]);  // XNOr xnor_3, 24 bits wide
  assign Enc[47:24] = xnor_3_out ^ xor_1_out;  // XOr xor_3, 24 bits wide

  // Other names for the same wires on the sheet: Key1[23:0] = Key[23:0]; Key2[23:0] = Key[35:12];
  //   Key3[23:0] = Key[47:24]
endmodule
