// Digital circuit circuit_2.5.dig as structural Verilog
module circuit_2_5 (
  input  [47:0] Plain_0,
  input  [47:0] Plain_1,
  input  [47:0] Plain_2,
  input  [47:0] Plain_3,
  input  [47:0] Key,
  input  [47:0] Plain_4,
  input  [47:0] Plain_5,
  input  [47:0] Plain_6,
  output [47:0] Ciph_3,
  output [47:0] Ciph_2,
  output [47:0] Ciph_1,
  output [47:0] Ciph_0,
  output [47:0] Ciph_4,
  output [47:0] Ciph_5,
  output [47:0] Ciph_6
);

  Block2 block2_1 (.Plain(Plain_6), .Key(Key), .Enc(Ciph_6));
  Block2 block2_2 (.Plain(Plain_5), .Key(Key), .Enc(Ciph_5));
  Block2 block2_3 (.Plain(Plain_4), .Key(Key), .Enc(Ciph_4));
  Block2 block2_4 (.Plain(Plain_3), .Key(Key), .Enc(Ciph_3));
  Block2 block2_5 (.Plain(Plain_2), .Key(Key), .Enc(Ciph_2));
  Block2 block2_6 (.Plain(Plain_1), .Key(Key), .Enc(Ciph_1));
  Block2 block2_7 (.Plain(Plain_0), .Key(Key), .Enc(Ciph_0));
endmodule
