// Digital circuit Block4 - SOLVE.dig as structural Verilog
module Block4___SOLVE (
  input  [63:0] Enc_r,
  input  [6:0] Ready,
  input  Clock,
  input  [6:0] Count,
  input  [63:0] In,
  output [63:0] Out
);

  wire and_3_out, and_4_out, bitselector_1_out, bitselector_2_out, bitselector_3_out, block4_1_p2,
       block4_1_p3, block4_2_p3, comparator_1_eq, comparator_2_eq, xnor_1_out, xnor_2_out, xor_1_out;
  wire [63:0] and_1_out, barrelshifter_1_out, barrelshifter_2_out, driver_1_out, or_1_out;

  BarrelShifter #(.Bits(64), .barrelShifterMode("rotate")) barrelshifter_1 (
    .in(64'hfffffffffffffffe), .shift(Count), .out(barrelshifter_1_out));
  assign and_1_out = barrelshifter_1_out & In;  // And and_1, 64 bits wide
  assign or_1_out = In | barrelshifter_2_out;  // Or or_1, 64 bits wide
  BarrelShifter #(.Bits(64), .barrelShifterMode("rotate")) barrelshifter_2 (
    .in(64'h1), .shift(Count), .out(barrelshifter_2_out));
  // Block4 block4_1: pin names not known; wires that end beside it: and_1_out, block4_1_p2, block4_1_p3
  // Block4 block4_2: pin names not known; wires that end beside it: or_1_out, block4_1_p2, block4_2_p3
  and and_2 (block4_1_p2, Clock, comparator_1_eq);
  Comparator #(.Bits(7)) comparator_1 (.a(Ready), .b(Count), .eq(comparator_1_eq));  // open: gt, lt
  // Probe on and_1_out
  BitSelector #(.Selector_Bits(6)) bitselector_1 (.in(block4_1_p3), .sel(Count[5:0]), .out(bitselector_1_out));
  BitSelector #(.Selector_Bits(6)) bitselector_2 (.in(block4_2_p3), .sel(Count[5:0]), .out(bitselector_2_out));
  xnor xnor_1 (xnor_1_out, bitselector_1_out, bitselector_3_out);
  xnor xnor_2 (xnor_2_out, bitselector_2_out, bitselector_3_out);
  BitSelector #(.Selector_Bits(6)) bitselector_3 (.in(Enc_r), .sel(Count[5:0]), .out(bitselector_3_out));
  xor xor_1 (xor_1_out, xnor_1_out, xnor_2_out);
  // Probe on or_1_out
  and and_3 (and_3_out, xor_1_out, xnor_1_out);
  and and_4 (and_4_out, xor_1_out, xnor_2_out);
  assign driver_1_out = and_3_out ? and_1_out : 64'bz;  // Driver driver_1
  assign driver_1_out = and_4_out ? or_1_out : 64'bz;  // Driver driver_2
  assign Out = comparator_2_eq ? driver_1_out : 64'bz;  // Driver driver_3
  Comparator #(.Bits(7)) comparator_2 (.a(Ready), .b(Count), .eq(comparator_2_eq));  // open: gt, lt

  // Other names for the same wires on the sheet: En[63:0] = Enc_r

  // Notes on the sheet:
  //   Enc_r: default -1199087619387027561
  //   Ready: default 3
  //   Count: default 3
  //   In: default 7
endmodule
