// Digital circuit DE3_Solver.dig as structural Verilog
module DE3_Solver (
  input  Clock,
  input  Ready,
  input  [63:0] Enc_r,
  output [63:0] out_4,
  output [63:0] out_5,
  output [63:0] out_6,
  output [63:0] out_7,
  output [63:0] out_8,
  output [63:0] out_9,
  output [63:0] out_10,
  output [63:0] out_11,
  output [63:0] out_12,
  output [63:0] out_13,
  output [63:0] out_14,
  output [63:0] out_15,
  output [63:0] out_16,
  output [63:0] out_17,
  output [63:0] out_18,
  output [63:0] out_19,
  output [63:0] out_20,
  output [63:0] out_21,
  output [63:0] out_22,
  output [63:0] out_23,
  output [63:0] out_24,
  output [63:0] out_25,
  output [63:0] out_26,
  output [63:0] out_27,
  output [63:0] out_28,
  output [63:0] out_29,
  output [63:0] out_30,
  output [63:0] out_31,
  output [63:0] out_32,
  output [63:0] out_33,
  output [63:0] out_34,
  output [63:0] out_35,
  output [63:0] out_36,
  output [63:0] out_37,
  output [63:0] out_38,
  output [63:0] out_39,
  output [63:0] out_40,
  output [63:0] out_41,
  output [63:0] out_42,
  output [63:0] out_43,
  output [63:0] out_44,
  output [63:0] out_45,
  output [63:0] out_46,
  output [63:0] out_47,
  output [63:0] out_48,
  output [63:0] out_49,
  output [63:0] out_50,
  output [63:0] out_51,
  output [63:0] out_52,
  output [63:0] out_53,
  output [63:0] out_54,
  output [63:0] out_55,
  output [63:0] out_56,
  output [63:0] out_57,
  output [63:0] out_58,
  output [63:0] out_59,
  output [63:0] out_60,
  output [63:0] out_61,
  output [63:0] out_62,
  output [63:0] out_63,
  output [63:0] out_64,
  output [63:0] out_65,
  output [63:0] out_66,
  output [63:0] out_67
);

  wire C, comparator_1_eq, comparator_2_eq, comparator_3_eq, comparator_4_eq, comparator_5_eq,
       comparator_6_eq, comparator_7_eq, comparator_8_eq, comparator_9_eq, comparator_10_eq,
       comparator_11_eq, comparator_12_eq, comparator_13_eq, comparator_14_eq, comparator_15_eq,
       comparator_16_eq, comparator_17_eq, comparator_18_eq, comparator_19_eq, comparator_20_eq,
       comparator_21_eq, comparator_22_eq, comparator_23_eq, comparator_24_eq, comparator_25_eq,
       comparator_26_eq, comparator_27_eq, comparator_28_eq, comparator_29_eq, comparator_30_eq,
       comparator_31_eq, comparator_32_eq, comparator_33_eq, comparator_34_eq, comparator_35_eq,
       comparator_36_eq, comparator_37_eq, comparator_38_eq, comparator_39_eq, comparator_40_eq,
       comparator_41_eq, comparator_42_eq, comparator_43_eq, comparator_44_eq, comparator_45_eq,
       comparator_46_eq, comparator_47_eq, comparator_48_eq, comparator_49_eq, comparator_50_eq,
       comparator_51_eq, comparator_52_eq, comparator_53_eq, comparator_54_eq, comparator_55_eq,
       comparator_56_eq, comparator_57_eq, comparator_58_eq, comparator_59_eq, comparator_60_eq,
       comparator_61_eq, comparator_62_eq, comparator_63_eq, comparator_64_eq, driver_2_out, switch_1_b;
  wire [6:0] add_1_s, add_2_s, add_3_s, add_4_s, add_5_s, add_6_s, add_7_s, add_8_s, add_9_s, add_10_s,
       add_11_s, add_12_s, add_13_s, add_14_s, add_15_s, add_16_s, add_17_s, add_18_s, add_19_s, add_20_s,
       add_21_s, add_22_s, add_23_s, add_24_s, add_25_s, add_26_s, add_27_s, add_28_s, add_29_s, add_30_s,
       add_31_s, add_32_s, add_33_s, add_34_s, add_35_s, add_36_s, add_37_s, add_38_s, add_39_s, add_40_s,
       add_41_s, add_42_s, add_43_s, add_44_s, add_45_s, add_46_s, add_47_s, add_48_s, add_49_s, add_50_s,
       add_51_s, add_52_s, add_53_s, add_54_s, add_55_s, add_56_s, add_57_s, add_58_s, add_59_s, add_60_s,
       add_61_s, add_62_s, add_63_s, add_64_s, R;
  wire [63:0] block4___solve_1_out, block4___solve_2_out, block4___solve_3_out, block4___solve_4_out,
       block4___solve_5_out, block4___solve_6_out, block4___solve_7_out, block4___solve_8_out,
       block4___solve_9_out, block4___solve_10_out, block4___solve_11_out, block4___solve_12_out,
       block4___solve_13_out, block4___solve_14_out, block4___solve_15_out, block4___solve_16_out,
       block4___solve_17_out, block4___solve_18_out, block4___solve_19_out, block4___solve_20_out,
       block4___solve_21_out, block4___solve_22_out, block4___solve_23_out, block4___solve_24_out,
       block4___solve_25_out, block4___solve_26_out, block4___solve_27_out, block4___solve_28_out,
       block4___solve_29_out, block4___solve_30_out, block4___solve_31_out, block4___solve_32_out,
       block4___solve_33_out, block4___solve_34_out, block4___solve_35_out, block4___solve_36_out,
       block4___solve_37_out, block4___solve_38_out, block4___solve_39_out, block4___solve_40_out,
       block4___solve_41_out, block4___solve_42_out, block4___solve_43_out, block4___solve_44_out,
       block4___solve_45_out, block4___solve_46_out, block4___solve_47_out, block4___solve_48_out,
       block4___solve_49_out, block4___solve_50_out, block4___solve_51_out, block4___solve_52_out,
       block4___solve_53_out, block4___solve_54_out, block4___solve_55_out, block4___solve_56_out,
       block4___solve_57_out, block4___solve_58_out, block4___solve_59_out, block4___solve_60_out,
       block4___solve_61_out, block4___solve_62_out, block4___solve_63_out, block4___solve_64_out,
       driver_3_out, driver_4_out, driver_5_out, driver_6_out, driver_7_out, driver_8_out, driver_9_out,
       driver_10_out, driver_11_out, driver_12_out, driver_13_out, driver_14_out, driver_15_out,
       driver_16_out, driver_17_out, driver_18_out, driver_19_out, driver_20_out, driver_21_out,
       driver_22_out, driver_23_out, driver_24_out, driver_25_out, driver_26_out, driver_27_out,
       driver_28_out, driver_29_out, driver_30_out, driver_31_out, driver_32_out, driver_33_out,
       driver_34_out, driver_35_out, driver_36_out, driver_37_out, driver_38_out, driver_39_out,
       driver_40_out, driver_41_out, driver_42_out, driver_43_out, driver_44_out, driver_45_out,
       driver_46_out, driver_47_out, driver_48_out, driver_49_out, driver_50_out, driver_51_out,
       driver_52_out, driver_53_out, driver_54_out, driver_55_out, driver_56_out, driver_57_out,
       driver_58_out, driver_59_out, driver_60_out, driver_61_out, driver_62_out, driver_63_out,
       driver_64_out, driver_65_out, driver_66_out;

  Switch switch_1 (.A(1'b1), .B(switch_1_b));
  assign C = switch_1_b ? Clock : 1'bz;  // Driver driver_1
  assign driver_2_out = switch_1_b ? Ready : 1'bz;  // Driver driver_2
  PullDown pulldown_1 (.out(C));
  PullDown pulldown_2 (.out(driver_2_out));
  Add #(.Bits(7)) add_1 (.a({7{1'b0}}), .b({7{1'b0}}), .c_i(1'b0), .s(add_1_s));  // open: c_o
  Block4___SOLVE block4___solve_1 (
    .Clock(C), .Count(add_1_s), .Ready(R), .Enc_r(Enc_r), .Out(block4___solve_1_out), .In({64{1'b0}}));
  Add #(.Bits(7)) add_2 (.a(add_57_s), .b({7{1'b0}}), .c_i(1'b1), .s(add_2_s));  // open: c_o
  Block4___SOLVE block4___solve_2 (
    .Clock(C), .Count(add_2_s), .Ready(R), .Enc_r(Enc_r), .Out(block4___solve_2_out), .In(out_11));
  Add #(.Bits(7)) add_3 (.a(add_58_s), .b({7{1'b0}}), .c_i(1'b1), .s(add_3_s));  // open: c_o
  Block4___SOLVE block4___solve_3 (
    .Clock(C), .Count(add_3_s), .Ready(R), .Enc_r(Enc_r), .Out(block4___solve_3_out), .In(out_19));
  Add #(.Bits(7)) add_4 (.a(add_59_s), .b({7{1'b0}}), .c_i(1'b1), .s(add_4_s));  // open: c_o
  Block4___SOLVE block4___solve_4 (
    .Clock(C), .Count(add_4_s), .Ready(R), .Enc_r(Enc_r), .Out(block4___solve_4_out), .In(out_27));
  Add #(.Bits(7)) add_5 (.a(add_60_s), .b({7{1'b0}}), .c_i(1'b1), .s(add_5_s));  // open: c_o
  Block4___SOLVE block4___solve_5 (
    .Clock(C), .Count(add_5_s), .Ready(R), .Enc_r(Enc_r), .Out(block4___solve_5_out), .In(out_35));
  Add #(.Bits(7)) add_6 (.a(add_61_s), .b({7{1'b0}}), .c_i(1'b1), .s(add_6_s));  // open: c_o
  Block4___SOLVE block4___solve_6 (
    .Clock(C), .Count(add_6_s), .Ready(R), .Enc_r(Enc_r), .Out(block4___solve_6_out), .In(out_43));
  Add #(.Bits(7)) add_7 (.a(add_62_s), .b({7{1'b0}}), .c_i(1'b1), .s(add_7_s));  // open: c_o
  Block4___SOLVE block4___solve_7 (
    .Clock(C), .Count(add_7_s), .Ready(R), .Enc_r(Enc_r), .Out(block4___solve_7_out), .In(out_51));
  Add #(.Bits(7)) add_8 (.a(add_63_s), .b({7{1'b0}}), .c_i(1'b1), .s(add_8_s));  // open: c_o
  Block4___SOLVE block4___solve_8 (
    .Clock(C), .Count(add_8_s), .Ready(R), .Enc_r(Enc_r), .Out(block4___solve_8_out), .In(out_59));
  Counter #(.Bits(7)) counter_1 (.en(1'b1), .C(driver_2_out), .clr(1'b0), .out(R));  // open: ovf
  // Probe on add_1_s
  Comparator #(.Bits(7)) comparator_1 (.a(add_1_s), .b(R), .eq(comparator_1_eq));  // open: gt, lt
  // Probe on add_2_s
  Comparator #(.Bits(7)) comparator_2 (.a(add_2_s), .b(R), .eq(comparator_2_eq));  // open: gt, lt
  // Probe on add_3_s
  Comparator #(.Bits(7)) comparator_3 (.a(add_3_s), .b(R), .eq(comparator_3_eq));  // open: gt, lt
  // Probe on add_4_s
  Comparator #(.Bits(7)) comparator_4 (.a(add_4_s), .b(R), .eq(comparator_4_eq));  // open: gt, lt
  // Probe on add_5_s
  Comparator #(.Bits(7)) comparator_5 (.a(add_5_s), .b(R), .eq(comparator_5_eq));  // open: gt, lt
  // Probe on add_6_s
  Comparator #(.Bits(7)) comparator_6 (.a(add_6_s), .b(R), .eq(comparator_6_eq));  // open: gt, lt
  // Probe on add_7_s
  Comparator #(.Bits(7)) comparator_7 (.a(add_7_s), .b(R), .eq(comparator_7_eq));  // open: gt, lt
  // Probe on add_8_s
  Comparator #(.Bits(7)) comparator_8 (.a(add_8_s), .b(R), .eq(comparator_8_eq));  // open: gt, lt
  assign driver_3_out = comparator_1_eq ? block4___solve_1_out : 64'bz;  // Driver driver_3
  Register #(.Bits(64)) register_1 (.D(driver_3_out), .C(C), .en(comparator_1_eq), .Q(out_4));
  assign driver_4_out = comparator_2_eq ? block4___solve_2_out : 64'bz;  // Driver driver_4
  Register #(.Bits(64)) register_2 (.D(driver_4_out), .C(C), .en(comparator_2_eq), .Q(out_12));
  assign driver_5_out = comparator_3_eq ? block4___solve_3_out : 64'bz;  // Driver driver_5
  Register #(.Bits(64)) register_3 (.D(driver_5_out), .C(C), .en(comparator_3_eq), .Q(out_20));
  assign driver_6_out = comparator_4_eq ? block4___solve_4_out : 64'bz;  // Driver driver_6
  Register #(.Bits(64)) register_4 (.D(driver_6_out), .C(C), .en(comparator_4_eq), .Q(out_28));
  assign driver_7_out = comparator_5_eq ? block4___solve_5_out : 64'bz;  // Driver driver_7
  Register #(.Bits(64)) register_5 (.D(driver_7_out), .C(C), .en(comparator_5_eq), .Q(out_36));
  assign driver_8_out = comparator_6_eq ? block4___solve_6_out : 64'bz;  // Driver driver_8
  Register #(.Bits(64)) register_6 (.D(driver_8_out), .C(C), .en(comparator_6_eq), .Q(out_44));
  assign driver_9_out = comparator_7_eq ? block4___solve_7_out : 64'bz;  // Driver driver_9
  Register #(.Bits(64)) register_7 (.D(driver_9_out), .C(C), .en(comparator_7_eq), .Q(out_52));
  assign driver_10_out = comparator_8_eq ? block4___solve_8_out : 64'bz;  // Driver driver_10
  Register #(.Bits(64)) register_8 (.D(driver_10_out), .C(C), .en(comparator_8_eq), .Q(out_60));
  Add #(.Bits(7)) add_9 (.a(add_1_s), .b({7{1'b0}}), .c_i(1'b1), .s(add_9_s));  // open: c_o
  Add #(.Bits(7)) add_10 (.a(add_2_s), .b({7{1'b0}}), .c_i(1'b1), .s(add_10_s));  // open: c_o
  Add #(.Bits(7)) add_11 (.a(add_3_s), .b({7{1'b0}}), .c_i(1'b1), .s(add_11_s));  // open: c_o
  Add #(.Bits(7)) add_12 (.a(add_4_s), .b({7{1'b0}}), .c_i(1'b1), .s(add_12_s));  // open: c_o
  Add #(.Bits(7)) add_13 (.a(add_5_s), .b({7{1'b0}}), .c_i(1'b1), .s(add_13_s));  // open: c_o
  Add #(.Bits(7)) add_14 (.a(add_6_s), .b({7{1'b0}}), .c_i(1'b1), .s(add_14_s));  // open: c_o
  Add #(.Bits(7)) add_15 (.a(add_7_s), .b({7{1'b0}}), .c_i(1'b1), .s(add_15_s));  // open: c_o
  Add #(.Bits(7)) add_16 (.a(add_8_s), .b({7{1'b0}}), .c_i(1'b1), .s(add_16_s));  // open: c_o
  Block4___SOLVE block4___solve_9 (
    .Clock(C), .Count(add_9_s), .Ready(R), .Enc_r(Enc_r), .Out(block4___solve_9_out), .In(out_4));
  Comparator #(.Bits(7)) comparator_9 (.a(add_9_s), .b(R), .eq(comparator_9_eq));  // open: gt, lt
  Block4___SOLVE block4___solve_10 (
    .Clock(C), .Count(add_10_s), .Ready(R), .Enc_r(Enc_r), .Out(block4___solve_10_out), .In(out_12));
  Comparator #(.Bits(7)) comparator_10 (.a(add_10_s), .b(R), .eq(comparator_10_eq));  // open: gt, lt
  Block4___SOLVE block4___solve_11 (
    .Clock(C), .Count(add_11_s), .Ready(R), .Enc_r(Enc_r), .Out(block4___solve_11_out), .In(out_20));
  Comparator #(.Bits(7)) comparator_11 (.a(add_11_s), .b(R), .eq(comparator_11_eq));  // open: gt, lt
  Block4___SOLVE block4___solve_12 (
    .Clock(C), .Count(add_12_s), .Ready(R), .Enc_r(Enc_r), .Out(block4___solve_12_out), .In(out_28));
  Comparator #(.Bits(7)) comparator_12 (.a(add_12_s), .b(R), .eq(comparator_12_eq));  // open: gt, lt
  Block4___SOLVE block4___solve_13 (
    .Clock(C), .Count(add_13_s), .Ready(R), .Enc_r(Enc_r), .Out(block4___solve_13_out), .In(out_36));
  Comparator #(.Bits(7)) comparator_13 (.a(add_13_s), .b(R), .eq(comparator_13_eq));  // open: gt, lt
  Block4___SOLVE block4___solve_14 (
    .Clock(C), .Count(add_14_s), .Ready(R), .Enc_r(Enc_r), .Out(block4___solve_14_out), .In(out_44));
  Comparator #(.Bits(7)) comparator_14 (.a(add_14_s), .b(R), .eq(comparator_14_eq));  // open: gt, lt
  Block4___SOLVE block4___solve_15 (
    .Clock(C), .Count(add_15_s), .Ready(R), .Enc_r(Enc_r), .Out(block4___solve_15_out), .In(out_52));
  Comparator #(.Bits(7)) comparator_15 (.a(add_15_s), .b(R), .eq(comparator_15_eq));  // open: gt, lt
  Block4___SOLVE block4___solve_16 (
    .Clock(C), .Count(add_16_s), .Ready(R), .Enc_r(Enc_r), .Out(block4___solve_16_out), .In(out_60));
  Comparator #(.Bits(7)) comparator_16 (.a(add_16_s), .b(R), .eq(comparator_16_eq));  // open: gt, lt
  // Probe on add_9_s
  // Probe on add_10_s
  // Probe on add_11_s
  // Probe on add_12_s
  // Probe on add_13_s
  // Probe on add_14_s
  // Probe on add_15_s
  // Probe on add_16_s
  Add #(.Bits(7)) add_17 (.a(add_9_s), .b({7{1'b0}}), .c_i(1'b1), .s(add_17_s));  // open: c_o
  assign driver_11_out = comparator_9_eq ? block4___solve_9_out : 64'bz;  // Driver driver_11
  Register #(.Bits(64)) register_9 (.D(driver_11_out), .C(C), .en(comparator_9_eq), .Q(out_5));
  Add #(.Bits(7)) add_18 (.a(add_10_s), .b({7{1'b0}}), .c_i(1'b1), .s(add_18_s));  // open: c_o
  assign driver_12_out = comparator_10_eq ? block4___solve_10_out : 64'bz;  // Driver driver_12
  Register #(.Bits(64)) register_10 (.D(driver_12_out), .C(C), .en(comparator_10_eq), .Q(out_13));
  Add #(.Bits(7)) add_19 (.a(add_11_s), .b({7{1'b0}}), .c_i(1'b1), .s(add_19_s));  // open: c_o
  assign driver_13_out = comparator_11_eq ? block4___solve_11_out : 64'bz;  // Driver driver_13
  Register #(.Bits(64)) register_11 (.D(driver_13_out), .C(C), .en(comparator_11_eq), .Q(out_21));
  Add #(.Bits(7)) add_20 (.a(add_12_s), .b({7{1'b0}}), .c_i(1'b1), .s(add_20_s));  // open: c_o
  assign driver_14_out = comparator_12_eq ? block4___solve_12_out : 64'bz;  // Driver driver_14
  Register #(.Bits(64)) register_12 (.D(driver_14_out), .C(C), .en(comparator_12_eq), .Q(out_29));
  Add #(.Bits(7)) add_21 (.a(add_13_s), .b({7{1'b0}}), .c_i(1'b1), .s(add_21_s));  // open: c_o
  assign driver_15_out = comparator_13_eq ? block4___solve_13_out : 64'bz;  // Driver driver_15
  Register #(.Bits(64)) register_13 (.D(driver_15_out), .C(C), .en(comparator_13_eq), .Q(out_37));
  Add #(.Bits(7)) add_22 (.a(add_14_s), .b({7{1'b0}}), .c_i(1'b1), .s(add_22_s));  // open: c_o
  assign driver_16_out = comparator_14_eq ? block4___solve_14_out : 64'bz;  // Driver driver_16
  Register #(.Bits(64)) register_14 (.D(driver_16_out), .C(C), .en(comparator_14_eq), .Q(out_45));
  Add #(.Bits(7)) add_23 (.a(add_15_s), .b({7{1'b0}}), .c_i(1'b1), .s(add_23_s));  // open: c_o
  assign driver_17_out = comparator_15_eq ? block4___solve_15_out : 64'bz;  // Driver driver_17
  Register #(.Bits(64)) register_15 (.D(driver_17_out), .C(C), .en(comparator_15_eq), .Q(out_53));
  Add #(.Bits(7)) add_24 (.a(add_16_s), .b({7{1'b0}}), .c_i(1'b1), .s(add_24_s));  // open: c_o
  assign driver_18_out = comparator_16_eq ? block4___solve_16_out : 64'bz;  // Driver driver_18
  Register #(.Bits(64)) register_16 (.D(driver_18_out), .C(C), .en(comparator_16_eq), .Q(out_61));
  Block4___SOLVE block4___solve_17 (
    .Clock(C), .Count(add_17_s), .Ready(R), .Enc_r(Enc_r), .Out(block4___solve_17_out), .In(out_5));
  Comparator #(.Bits(7)) comparator_17 (.a(add_17_s), .b(R), .eq(comparator_17_eq));  // open: gt, lt
  Block4___SOLVE block4___solve_18 (
    .Clock(C), .Count(add_18_s), .Ready(R), .Enc_r(Enc_r), .Out(block4___solve_18_out), .In(out_13));
  Comparator #(.Bits(7)) comparator_18 (.a(add_18_s), .b(R), .eq(comparator_18_eq));  // open: gt, lt
  Block4___SOLVE block4___solve_19 (
    .Clock(C), .Count(add_19_s), .Ready(R), .Enc_r(Enc_r), .Out(block4___solve_19_out), .In(out_21));
  Comparator #(.Bits(7)) comparator_19 (.a(add_19_s), .b(R), .eq(comparator_19_eq));  // open: gt, lt
  Block4___SOLVE block4___solve_20 (
    .Clock(C), .Count(add_20_s), .Ready(R), .Enc_r(Enc_r), .Out(block4___solve_20_out), .In(out_29));
  Comparator #(.Bits(7)) comparator_20 (.a(add_20_s), .b(R), .eq(comparator_20_eq));  // open: gt, lt
  Block4___SOLVE block4___solve_21 (
    .Clock(C), .Count(add_21_s), .Ready(R), .Enc_r(Enc_r), .Out(block4___solve_21_out), .In(out_37));
  Comparator #(.Bits(7)) comparator_21 (.a(add_21_s), .b(R), .eq(comparator_21_eq));  // open: gt, lt
  Block4___SOLVE block4___solve_22 (
    .Clock(C), .Count(add_22_s), .Ready(R), .Enc_r(Enc_r), .Out(block4___solve_22_out), .In(out_45));
  Comparator #(.Bits(7)) comparator_22 (.a(add_22_s), .b(R), .eq(comparator_22_eq));  // open: gt, lt
  Block4___SOLVE block4___solve_23 (
    .Clock(C), .Count(add_23_s), .Ready(R), .Enc_r(Enc_r), .Out(block4___solve_23_out), .In(out_53));
  Comparator #(.Bits(7)) comparator_23 (.a(add_23_s), .b(R), .eq(comparator_23_eq));  // open: gt, lt
  Block4___SOLVE block4___solve_24 (
    .Clock(C), .Count(add_24_s), .Ready(R), .Enc_r(Enc_r), .Out(block4___solve_24_out), .In(out_61));
  Comparator #(.Bits(7)) comparator_24 (.a(add_24_s), .b(R), .eq(comparator_24_eq));  // open: gt, lt
  // Probe on add_17_s
  // Probe on add_18_s
  // Probe on add_19_s
  // Probe on add_20_s
  // Probe on add_21_s
  // Probe on add_22_s
  // Probe on add_23_s
  // Probe on add_24_s
  assign driver_19_out = comparator_17_eq ? block4___solve_17_out : 64'bz;  // Driver driver_19
  Register #(.Bits(64)) register_17 (.D(driver_19_out), .C(C), .en(comparator_17_eq), .Q(out_6));
  assign driver_20_out = comparator_18_eq ? block4___solve_18_out : 64'bz;  // Driver driver_20
  Register #(.Bits(64)) register_18 (.D(driver_20_out), .C(C), .en(comparator_18_eq), .Q(out_14));
  assign driver_21_out = comparator_19_eq ? block4___solve_19_out : 64'bz;  // Driver driver_21
  Register #(.Bits(64)) register_19 (.D(driver_21_out), .C(C), .en(comparator_19_eq), .Q(out_22));
  assign driver_22_out = comparator_20_eq ? block4___solve_20_out : 64'bz;  // Driver driver_22
  Register #(.Bits(64)) register_20 (.D(driver_22_out), .C(C), .en(comparator_20_eq), .Q(out_30));
  assign driver_23_out = comparator_21_eq ? block4___solve_21_out : 64'bz;  // Driver driver_23
  Register #(.Bits(64)) register_21 (.D(driver_23_out), .C(C), .en(comparator_21_eq), .Q(out_38));
  assign driver_24_out = comparator_22_eq ? block4___solve_22_out : 64'bz;  // Driver driver_24
  Register #(.Bits(64)) register_22 (.D(driver_24_out), .C(C), .en(comparator_22_eq), .Q(out_46));
  assign driver_25_out = comparator_23_eq ? block4___solve_23_out : 64'bz;  // Driver driver_25
  Register #(.Bits(64)) register_23 (.D(driver_25_out), .C(C), .en(comparator_23_eq), .Q(out_54));
  assign driver_26_out = comparator_24_eq ? block4___solve_24_out : 64'bz;  // Driver driver_26
  Register #(.Bits(64)) register_24 (.D(driver_26_out), .C(C), .en(comparator_24_eq), .Q(out_62));
  Add #(.Bits(7)) add_25 (.a(add_17_s), .b({7{1'b0}}), .c_i(1'b1), .s(add_25_s));  // open: c_o
  Block4___SOLVE block4___solve_25 (
    .Clock(C), .Count(add_25_s), .Ready(R), .Enc_r(Enc_r), .Out(block4___solve_25_out), .In(out_6));
  Add #(.Bits(7)) add_26 (.a(add_18_s), .b({7{1'b0}}), .c_i(1'b1), .s(add_26_s));  // open: c_o
  Block4___SOLVE block4___solve_26 (
    .Clock(C), .Count(add_26_s), .Ready(R), .Enc_r(Enc_r), .Out(block4___solve_26_out), .In(out_14));
  Add #(.Bits(7)) add_27 (.a(add_19_s), .b({7{1'b0}}), .c_i(1'b1), .s(add_27_s));  // open: c_o
  Block4___SOLVE block4___solve_27 (
    .Clock(C), .Count(add_27_s), .Ready(R), .Enc_r(Enc_r), .Out(block4___solve_27_out), .In(out_22));
  Add #(.Bits(7)) add_28 (.a(add_20_s), .b({7{1'b0}}), .c_i(1'b1), .s(add_28_s));  // open: c_o
  Block4___SOLVE block4___solve_28 (
    .Clock(C), .Count(add_28_s), .Ready(R), .Enc_r(Enc_r), .Out(block4___solve_28_out), .In(out_30));
  Add #(.Bits(7)) add_29 (.a(add_21_s), .b({7{1'b0}}), .c_i(1'b1), .s(add_29_s));  // open: c_o
  Block4___SOLVE block4___solve_29 (
    .Clock(C), .Count(add_29_s), .Ready(R), .Enc_r(Enc_r), .Out(block4___solve_29_out), .In(out_38));
  Add #(.Bits(7)) add_30 (.a(add_22_s), .b({7{1'b0}}), .c_i(1'b1), .s(add_30_s));  // open: c_o
  Block4___SOLVE block4___solve_30 (
    .Clock(C), .Count(add_30_s), .Ready(R), .Enc_r(Enc_r), .Out(block4___solve_30_out), .In(out_46));
  Add #(.Bits(7)) add_31 (.a(add_23_s), .b({7{1'b0}}), .c_i(1'b1), .s(add_31_s));  // open: c_o
  Block4___SOLVE block4___solve_31 (
    .Clock(C), .Count(add_31_s), .Ready(R), .Enc_r(Enc_r), .Out(block4___solve_31_out), .In(out_54));
  Add #(.Bits(7)) add_32 (.a(add_24_s), .b({7{1'b0}}), .c_i(1'b1), .s(add_32_s));  // open: c_o
  Block4___SOLVE block4___solve_32 (
    .Clock(C), .Count(add_32_s), .Ready(R), .Enc_r(Enc_r), .Out(block4___solve_32_out), .In(out_62));
  // Probe on add_25_s
  Comparator #(.Bits(7)) comparator_25 (.a(add_25_s), .b(R), .eq(comparator_25_eq));  // open: gt, lt
  // Probe on add_26_s
  Comparator #(.Bits(7)) comparator_26 (.a(add_26_s), .b(R), .eq(comparator_26_eq));  // open: gt, lt
  // Probe on add_27_s
  Comparator #(.Bits(7)) comparator_27 (.a(add_27_s), .b(R), .eq(comparator_27_eq));  // open: gt, lt
  // Probe on add_28_s
  Comparator #(.Bits(7)) comparator_28 (.a(add_28_s), .b(R), .eq(comparator_28_eq));  // open: gt, lt
  // Probe on add_29_s
  Comparator #(.Bits(7)) comparator_29 (.a(add_29_s), .b(R), .eq(comparator_29_eq));  // open: gt, lt
  // Probe on add_30_s
  Comparator #(.Bits(7)) comparator_30 (.a(add_30_s), .b(R), .eq(comparator_30_eq));  // open: gt, lt
  // Probe on add_31_s
  Comparator #(.Bits(7)) comparator_31 (.a(add_31_s), .b(R), .eq(comparator_31_eq));  // open: gt, lt
  // Probe on add_32_s
  Comparator #(.Bits(7)) comparator_32 (.a(add_32_s), .b(R), .eq(comparator_32_eq));  // open: gt, lt
  assign driver_27_out = comparator_25_eq ? block4___solve_25_out : 64'bz;  // Driver driver_27
  Register #(.Bits(64)) register_25 (.D(driver_27_out), .C(C), .en(comparator_25_eq), .Q(out_7));
  assign driver_28_out = comparator_26_eq ? block4___solve_26_out : 64'bz;  // Driver driver_28
  Register #(.Bits(64)) register_26 (.D(driver_28_out), .C(C), .en(comparator_26_eq), .Q(out_15));
  assign driver_29_out = comparator_27_eq ? block4___solve_27_out : 64'bz;  // Driver driver_29
  Register #(.Bits(64)) register_27 (.D(driver_29_out), .C(C), .en(comparator_27_eq), .Q(out_23));
  assign driver_30_out = comparator_28_eq ? block4___solve_28_out : 64'bz;  // Driver driver_30
  Register #(.Bits(64)) register_28 (.D(driver_30_out), .C(C), .en(comparator_28_eq), .Q(out_31));
  assign driver_31_out = comparator_29_eq ? block4___solve_29_out : 64'bz;  // Driver driver_31
  Register #(.Bits(64)) register_29 (.D(driver_31_out), .C(C), .en(comparator_29_eq), .Q(out_39));
  assign driver_32_out = comparator_30_eq ? block4___solve_30_out : 64'bz;  // Driver driver_32
  Register #(.Bits(64)) register_30 (.D(driver_32_out), .C(C), .en(comparator_30_eq), .Q(out_47));
  assign driver_33_out = comparator_31_eq ? block4___solve_31_out : 64'bz;  // Driver driver_33
  Register #(.Bits(64)) register_31 (.D(driver_33_out), .C(C), .en(comparator_31_eq), .Q(out_55));
  assign driver_34_out = comparator_32_eq ? block4___solve_32_out : 64'bz;  // Driver driver_34
  Register #(.Bits(64)) register_32 (.D(driver_34_out), .C(C), .en(comparator_32_eq), .Q(out_63));
  Add #(.Bits(7)) add_33 (.a(add_25_s), .b({7{1'b0}}), .c_i(1'b1), .s(add_33_s));  // open: c_o
  Block4___SOLVE block4___solve_33 (
    .Clock(C), .Count(add_33_s), .Ready(R), .Enc_r(Enc_r), .Out(block4___solve_33_out), .In(out_7));
  Add #(.Bits(7)) add_34 (.a(add_26_s), .b({7{1'b0}}), .c_i(1'b1), .s(add_34_s));  // open: c_o
  Block4___SOLVE block4___solve_34 (
    .Clock(C), .Count(add_34_s), .Ready(R), .Enc_r(Enc_r), .Out(block4___solve_34_out), .In(out_15));
  Add #(.Bits(7)) add_35 (.a(add_27_s), .b({7{1'b0}}), .c_i(1'b1), .s(add_35_s));  // open: c_o
  Block4___SOLVE block4___solve_35 (
    .Clock(C), .Count(add_35_s), .Ready(R), .Enc_r(Enc_r), .Out(block4___solve_35_out), .In(out_23));
  Add #(.Bits(7)) add_36 (.a(add_28_s), .b({7{1'b0}}), .c_i(1'b1), .s(add_36_s));  // open: c_o
  Block4___SOLVE block4___solve_36 (
    .Clock(C), .Count(add_36_s), .Ready(R), .Enc_r(Enc_r), .Out(block4___solve_36_out), .In(out_31));
  Add #(.Bits(7)) add_37 (.a(add_29_s), .b({7{1'b0}}), .c_i(1'b1), .s(add_37_s));  // open: c_o
  Block4___SOLVE block4___solve_37 (
    .Clock(C), .Count(add_37_s), .Ready(R), .Enc_r(Enc_r), .Out(block4___solve_37_out), .In(out_39));
  Add #(.Bits(7)) add_38 (.a(add_30_s), .b({7{1'b0}}), .c_i(1'b1), .s(add_38_s));  // open: c_o
  Block4___SOLVE block4___solve_38 (
    .Clock(C), .Count(add_38_s), .Ready(R), .Enc_r(Enc_r), .Out(block4___solve_38_out), .In(out_47));
  Add #(.Bits(7)) add_39 (.a(add_31_s), .b({7{1'b0}}), .c_i(1'b1), .s(add_39_s));  // open: c_o
  Block4___SOLVE block4___solve_39 (
    .Clock(C), .Count(add_39_s), .Ready(R), .Enc_r(Enc_r), .Out(block4___solve_39_out), .In(out_55));
  Add #(.Bits(7)) add_40 (.a(add_32_s), .b({7{1'b0}}), .c_i(1'b1), .s(add_40_s));  // open: c_o
  Block4___SOLVE block4___solve_40 (
    .Clock(C), .Count(add_40_s), .Ready(R), .Enc_r(Enc_r), .Out(block4___solve_40_out), .In(out_63));
  // Probe on add_33_s
  Comparator #(.Bits(7)) comparator_33 (.a(add_33_s), .b(R), .eq(comparator_33_eq));  // open: gt, lt
  // Probe on add_34_s
  Comparator #(.Bits(7)) comparator_34 (.a(add_34_s), .b(R), .eq(comparator_34_eq));  // open: gt, lt
  // Probe on add_35_s
  Comparator #(.Bits(7)) comparator_35 (.a(add_35_s), .b(R), .eq(comparator_35_eq));  // open: gt, lt
  // Probe on add_36_s
  Comparator #(.Bits(7)) comparator_36 (.a(add_36_s), .b(R), .eq(comparator_36_eq));  // open: gt, lt
  // Probe on add_37_s
  Comparator #(.Bits(7)) comparator_37 (.a(add_37_s), .b(R), .eq(comparator_37_eq));  // open: gt, lt
  // Probe on add_38_s
  Comparator #(.Bits(7)) comparator_38 (.a(add_38_s), .b(R), .eq(comparator_38_eq));  // open: gt, lt
  // Probe on add_39_s
  Comparator #(.Bits(7)) comparator_39 (.a(add_39_s), .b(R), .eq(comparator_39_eq));  // open: gt, lt
  // Probe on add_40_s
  Comparator #(.Bits(7)) comparator_40 (.a(add_40_s), .b(R), .eq(comparator_40_eq));  // open: gt, lt
  assign driver_35_out = comparator_33_eq ? block4___solve_33_out : 64'bz;  // Driver driver_35
  Register #(.Bits(64)) register_33 (.D(driver_35_out), .C(C), .en(comparator_33_eq), .Q(out_8));
  assign driver_36_out = comparator_34_eq ? block4___solve_34_out : 64'bz;  // Driver driver_36
  Register #(.Bits(64)) register_34 (.D(driver_36_out), .C(C), .en(comparator_34_eq), .Q(out_16));
  assign driver_37_out = comparator_35_eq ? block4___solve_35_out : 64'bz;  // Driver driver_37
  Register #(.Bits(64)) register_35 (.D(driver_37_out), .C(C), .en(comparator_35_eq), .Q(out_24));
  assign driver_38_out = comparator_36_eq ? block4___solve_36_out : 64'bz;  // Driver driver_38
  Register #(.Bits(64)) register_36 (.D(driver_38_out), .C(C), .en(comparator_36_eq), .Q(out_32));
  assign driver_39_out = comparator_37_eq ? block4___solve_37_out : 64'bz;  // Driver driver_39
  Register #(.Bits(64)) register_37 (.D(driver_39_out), .C(C), .en(comparator_37_eq), .Q(out_40));
  assign driver_40_out = comparator_38_eq ? block4___solve_38_out : 64'bz;  // Driver driver_40
  Register #(.Bits(64)) register_38 (.D(driver_40_out), .C(C), .en(comparator_38_eq), .Q(out_48));
  assign driver_41_out = comparator_39_eq ? block4___solve_39_out : 64'bz;  // Driver driver_41
  Register #(.Bits(64)) register_39 (.D(driver_41_out), .C(C), .en(comparator_39_eq), .Q(out_56));
  assign driver_42_out = comparator_40_eq ? block4___solve_40_out : 64'bz;  // Driver driver_42
  Register #(.Bits(64)) register_40 (.D(driver_42_out), .C(C), .en(comparator_40_eq), .Q(out_64));
  Add #(.Bits(7)) add_41 (.a(add_33_s), .b({7{1'b0}}), .c_i(1'b1), .s(add_41_s));  // open: c_o
  Add #(.Bits(7)) add_42 (.a(add_34_s), .b({7{1'b0}}), .c_i(1'b1), .s(add_42_s));  // open: c_o
  Add #(.Bits(7)) add_43 (.a(add_35_s), .b({7{1'b0}}), .c_i(1'b1), .s(add_43_s));  // open: c_o
  Add #(.Bits(7)) add_44 (.a(add_36_s), .b({7{1'b0}}), .c_i(1'b1), .s(add_44_s));  // open: c_o
  Add #(.Bits(7)) add_45 (.a(add_37_s), .b({7{1'b0}}), .c_i(1'b1), .s(add_45_s));  // open: c_o
  Add #(.Bits(7)) add_46 (.a(add_38_s), .b({7{1'b0}}), .c_i(1'b1), .s(add_46_s));  // open: c_o
  Add #(.Bits(7)) add_47 (.a(add_39_s), .b({7{1'b0}}), .c_i(1'b1), .s(add_47_s));  // open: c_o
  Add #(.Bits(7)) add_48 (.a(add_40_s), .b({7{1'b0}}), .c_i(1'b1), .s(add_48_s));  // open: c_o
  Block4___SOLVE block4___solve_41 (
    .Clock(C), .Count(add_41_s), .Ready(R), .Enc_r(Enc_r), .Out(block4___solve_41_out), .In(out_8));
  Comparator #(.Bits(7)) comparator_41 (.a(add_41_s), .b(R), .eq(comparator_41_eq));  // open: gt, lt
  Block4___SOLVE block4___solve_42 (
    .Clock(C), .Count(add_42_s), .Ready(R), .Enc_r(Enc_r), .Out(block4___solve_42_out), .In(out_16));
  Comparator #(.Bits(7)) comparator_42 (.a(add_42_s), .b(R), .eq(comparator_42_eq));  // open: gt, lt
  Block4___SOLVE block4___solve_43 (
    .Clock(C), .Count(add_43_s), .Ready(R), .Enc_r(Enc_r), .Out(block4___solve_43_out), .In(out_24));
  Comparator #(.Bits(7)) comparator_43 (.a(add_43_s), .b(R), .eq(comparator_43_eq));  // open: gt, lt
  Block4___SOLVE block4___solve_44 (
    .Clock(C), .Count(add_44_s), .Ready(R), .Enc_r(Enc_r), .Out(block4___solve_44_out), .In(out_32));
  Comparator #(.Bits(7)) comparator_44 (.a(add_44_s), .b(R), .eq(comparator_44_eq));  // open: gt, lt
  Block4___SOLVE block4___solve_45 (
    .Clock(C), .Count(add_45_s), .Ready(R), .Enc_r(Enc_r), .Out(block4___solve_45_out), .In(out_40));
  Comparator #(.Bits(7)) comparator_45 (.a(add_45_s), .b(R), .eq(comparator_45_eq));  // open: gt, lt
  Block4___SOLVE block4___solve_46 (
    .Clock(C), .Count(add_46_s), .Ready(R), .Enc_r(Enc_r), .Out(block4___solve_46_out), .In(out_48));
  Comparator #(.Bits(7)) comparator_46 (.a(add_46_s), .b(R), .eq(comparator_46_eq));  // open: gt, lt
  Block4___SOLVE block4___solve_47 (
    .Clock(C), .Count(add_47_s), .Ready(R), .Enc_r(Enc_r), .Out(block4___solve_47_out), .In(out_56));
  Comparator #(.Bits(7)) comparator_47 (.a(add_47_s), .b(R), .eq(comparator_47_eq));  // open: gt, lt
  Block4___SOLVE block4___solve_48 (
    .Clock(C), .Count(add_48_s), .Ready(R), .Enc_r(Enc_r), .Out(block4___solve_48_out), .In(out_64));
  Comparator #(.Bits(7)) comparator_48 (.a(add_48_s), .b(R), .eq(comparator_48_eq));  // open: gt, lt
  // Probe on add_41_s
  // Probe on add_42_s
  // Probe on add_43_s
  // Probe on add_44_s
  // Probe on add_45_s
  // Probe on add_46_s
  // Probe on add_47_s
  // Probe on add_48_s
  Add #(.Bits(7)) add_49 (.a(add_41_s), .b({7{1'b0}}), .c_i(1'b1), .s(add_49_s));  // open: c_o
  assign driver_43_out = comparator_41_eq ? block4___solve_41_out : 64'bz;  // Driver driver_43
  Register #(.Bits(64)) register_41 (.D(driver_43_out), .C(C), .en(comparator_41_eq), .Q(out_9));
  Add #(.Bits(7)) add_50 (.a(add_42_s), .b({7{1'b0}}), .c_i(1'b1), .s(add_50_s));  // open: c_o
  assign driver_44_out = comparator_42_eq ? block4___solve_42_out : 64'bz;  // Driver driver_44
  Register #(.Bits(64)) register_42 (.D(driver_44_out), .C(C), .en(comparator_42_eq), .Q(out_17));
  Add #(.Bits(7)) add_51 (.a(add_43_s), .b({7{1'b0}}), .c_i(1'b1), .s(add_51_s));  // open: c_o
  assign driver_45_out = comparator_43_eq ? block4___solve_43_out : 64'bz;  // Driver driver_45
  Register #(.Bits(64)) register_43 (.D(driver_45_out), .C(C), .en(comparator_43_eq), .Q(out_25));
  Add #(.Bits(7)) add_52 (.a(add_44_s), .b({7{1'b0}}), .c_i(1'b1), .s(add_52_s));  // open: c_o
  assign driver_46_out = comparator_44_eq ? block4___solve_44_out : 64'bz;  // Driver driver_46
  Register #(.Bits(64)) register_44 (.D(driver_46_out), .C(C), .en(comparator_44_eq), .Q(out_33));
  Add #(.Bits(7)) add_53 (.a(add_45_s), .b({7{1'b0}}), .c_i(1'b1), .s(add_53_s));  // open: c_o
  assign driver_47_out = comparator_45_eq ? block4___solve_45_out : 64'bz;  // Driver driver_47
  Register #(.Bits(64)) register_45 (.D(driver_47_out), .C(C), .en(comparator_45_eq), .Q(out_41));
  Add #(.Bits(7)) add_54 (.a(add_46_s), .b({7{1'b0}}), .c_i(1'b1), .s(add_54_s));  // open: c_o
  assign driver_48_out = comparator_46_eq ? block4___solve_46_out : 64'bz;  // Driver driver_48
  Register #(.Bits(64)) register_46 (.D(driver_48_out), .C(C), .en(comparator_46_eq), .Q(out_49));
  Add #(.Bits(7)) add_55 (.a(add_47_s), .b({7{1'b0}}), .c_i(1'b1), .s(add_55_s));  // open: c_o
  assign driver_49_out = comparator_47_eq ? block4___solve_47_out : 64'bz;  // Driver driver_49
  Register #(.Bits(64)) register_47 (.D(driver_49_out), .C(C), .en(comparator_47_eq), .Q(out_57));
  Add #(.Bits(7)) add_56 (.a(add_48_s), .b({7{1'b0}}), .c_i(1'b1), .s(add_56_s));  // open: c_o
  assign driver_50_out = comparator_48_eq ? block4___solve_48_out : 64'bz;  // Driver driver_50
  Register #(.Bits(64)) register_48 (.D(driver_50_out), .C(C), .en(comparator_48_eq), .Q(out_65));
  Block4___SOLVE block4___solve_49 (
    .Clock(C), .Count(add_49_s), .Ready(R), .Enc_r(Enc_r), .Out(block4___solve_49_out), .In(out_9));
  Comparator #(.Bits(7)) comparator_49 (.a(add_49_s), .b(R), .eq(comparator_49_eq));  // open: gt, lt
  Block4___SOLVE block4___solve_50 (
    .Clock(C), .Count(add_50_s), .Ready(R), .Enc_r(Enc_r), .Out(block4___solve_50_out), .In(out_17));
  Comparator #(.Bits(7)) comparator_50 (.a(add_50_s), .b(R), .eq(comparator_50_eq));  // open: gt, lt
  Block4___SOLVE block4___solve_51 (
    .Clock(C), .Count(add_51_s), .Ready(R), .Enc_r(Enc_r), .Out(block4___solve_51_out), .In(out_25));
  Comparator #(.Bits(7)) comparator_51 (.a(add_51_s), .b(R), .eq(comparator_51_eq));  // open: gt, lt
  Block4___SOLVE block4___solve_52 (
    .Clock(C), .Count(add_52_s), .Ready(R), .Enc_r(Enc_r), .Out(block4___solve_52_out), .In(out_33));
  Comparator #(.Bits(7)) comparator_52 (.a(add_52_s), .b(R), .eq(comparator_52_eq));  // open: gt, lt
  Block4___SOLVE block4___solve_53 (
    .Clock(C), .Count(add_53_s), .Ready(R), .Enc_r(Enc_r), .Out(block4___solve_53_out), .In(out_41));
  Comparator #(.Bits(7)) comparator_53 (.a(add_53_s), .b(R), .eq(comparator_53_eq));  // open: gt, lt
  Block4___SOLVE block4___solve_54 (
    .Clock(C), .Count(add_54_s), .Ready(R), .Enc_r(Enc_r), .Out(block4___solve_54_out), .In(out_49));
  Comparator #(.Bits(7)) comparator_54 (.a(add_54_s), .b(R), .eq(comparator_54_eq));  // open: gt, lt
  Block4___SOLVE block4___solve_55 (
    .Clock(C), .Count(add_55_s), .Ready(R), .Enc_r(Enc_r), .Out(block4___solve_55_out), .In(out_57));
  Comparator #(.Bits(7)) comparator_55 (.a(add_55_s), .b(R), .eq(comparator_55_eq));  // open: gt, lt
  Block4___SOLVE block4___solve_56 (
    .Clock(C), .Count(add_56_s), .Ready(R), .Enc_r(Enc_r), .Out(block4___solve_56_out), .In(out_65));
  Comparator #(.Bits(7)) comparator_56 (.a(add_56_s), .b(R), .eq(comparator_56_eq));  // open: gt, lt
  // Probe on add_49_s
  // Probe on add_50_s
  // Probe on add_51_s
  // Probe on add_52_s
  // Probe on add_53_s
  // Probe on add_54_s
  // Probe on add_55_s
  // Probe on add_56_s
  assign driver_51_out = comparator_49_eq ? block4___solve_49_out : 64'bz;  // Driver driver_51
  Register #(.Bits(64)) register_49 (.D(driver_51_out), .C(C), .en(comparator_49_eq), .Q(out_10));
  assign driver_52_out = comparator_50_eq ? block4___solve_50_out : 64'bz;  // Driver driver_52
  Register #(.Bits(64)) register_50 (.D(driver_52_out), .C(C), .en(comparator_50_eq), .Q(out_18));
  assign driver_53_out = comparator_51_eq ? block4___solve_51_out : 64'bz;  // Driver driver_53
  Register #(.Bits(64)) register_51 (.D(driver_53_out), .C(C), .en(comparator_51_eq), .Q(out_26));
  assign driver_54_out = comparator_52_eq ? block4___solve_52_out : 64'bz;  // Driver driver_54
  Register #(.Bits(64)) register_52 (.D(driver_54_out), .C(C), .en(comparator_52_eq), .Q(out_34));
  assign driver_55_out = comparator_53_eq ? block4___solve_53_out : 64'bz;  // Driver driver_55
  Register #(.Bits(64)) register_53 (.D(driver_55_out), .C(C), .en(comparator_53_eq), .Q(out_42));
  assign driver_56_out = comparator_54_eq ? block4___solve_54_out : 64'bz;  // Driver driver_56
  Register #(.Bits(64)) register_54 (.D(driver_56_out), .C(C), .en(comparator_54_eq), .Q(out_50));
  assign driver_57_out = comparator_55_eq ? block4___solve_55_out : 64'bz;  // Driver driver_57
  Register #(.Bits(64)) register_55 (.D(driver_57_out), .C(C), .en(comparator_55_eq), .Q(out_58));
  assign driver_58_out = comparator_56_eq ? block4___solve_56_out : 64'bz;  // Driver driver_58
  Register #(.Bits(64)) register_56 (.D(driver_58_out), .C(C), .en(comparator_56_eq), .Q(out_66));
  Add #(.Bits(7)) add_57 (.a(add_49_s), .b({7{1'b0}}), .c_i(1'b1), .s(add_57_s));  // open: c_o
  Block4___SOLVE block4___solve_57 (
    .Clock(C), .Count(add_57_s), .Ready(R), .Enc_r(Enc_r), .Out(block4___solve_57_out), .In(out_10));
  Add #(.Bits(7)) add_58 (.a(add_50_s), .b({7{1'b0}}), .c_i(1'b1), .s(add_58_s));  // open: c_o
  Block4___SOLVE block4___solve_58 (
    .Clock(C), .Count(add_58_s), .Ready(R), .Enc_r(Enc_r), .Out(block4___solve_58_out), .In(out_18));
  Add #(.Bits(7)) add_59 (.a(add_51_s), .b({7{1'b0}}), .c_i(1'b1), .s(add_59_s));  // open: c_o
  Block4___SOLVE block4___solve_59 (
    .Clock(C), .Count(add_59_s), .Ready(R), .Enc_r(Enc_r), .Out(block4___solve_59_out), .In(out_26));
  Add #(.Bits(7)) add_60 (.a(add_52_s), .b({7{1'b0}}), .c_i(1'b1), .s(add_60_s));  // open: c_o
  Block4___SOLVE block4___solve_60 (
    .Clock(C), .Count(add_60_s), .Ready(R), .Enc_r(Enc_r), .Out(block4___solve_60_out), .In(out_34));
  Add #(.Bits(7)) add_61 (.a(add_53_s), .b({7{1'b0}}), .c_i(1'b1), .s(add_61_s));  // open: c_o
  Block4___SOLVE block4___solve_61 (
    .Clock(C), .Count(add_61_s), .Ready(R), .Enc_r(Enc_r), .Out(block4___solve_61_out), .In(out_42));
  Add #(.Bits(7)) add_62 (.a(add_54_s), .b({7{1'b0}}), .c_i(1'b1), .s(add_62_s));  // open: c_o
  Block4___SOLVE block4___solve_62 (
    .Clock(C), .Count(add_62_s), .Ready(R), .Enc_r(Enc_r), .Out(block4___solve_62_out), .In(out_50));
  Add #(.Bits(7)) add_63 (.a(add_55_s), .b({7{1'b0}}), .c_i(1'b1), .s(add_63_s));  // open: c_o
  Block4___SOLVE block4___solve_63 (
    .Clock(C), .Count(add_63_s), .Ready(R), .Enc_r(Enc_r), .Out(block4___solve_63_out), .In(out_58));
  Add #(.Bits(7)) add_64 (.a(add_56_s), .b({7{1'b0}}), .c_i(1'b1), .s(add_64_s));  // open: c_o
  Block4___SOLVE block4___solve_64 (
    .Clock(C), .Count(add_64_s), .Ready(R), .Enc_r(Enc_r), .Out(block4___solve_64_out), .In(out_66));
  // Probe on add_57_s
  Comparator #(.Bits(7)) comparator_57 (.a(add_57_s), .b(R), .eq(comparator_57_eq));  // open: gt, lt
  // Probe on add_58_s
  Comparator #(.Bits(7)) comparator_58 (.a(add_58_s), .b(R), .eq(comparator_58_eq));  // open: gt, lt
  // Probe on add_59_s
  Comparator #(.Bits(7)) comparator_59 (.a(add_59_s), .b(R), .eq(comparator_59_eq));  // open: gt, lt
  // Probe on add_60_s
  Comparator #(.Bits(7)) comparator_60 (.a(add_60_s), .b(R), .eq(comparator_60_eq));  // open: gt, lt
  // Probe on add_61_s
  Comparator #(.Bits(7)) comparator_61 (.a(add_61_s), .b(R), .eq(comparator_61_eq));  // open: gt, lt
  // Probe on add_62_s
  Comparator #(.Bits(7)) comparator_62 (.a(add_62_s), .b(R), .eq(comparator_62_eq));  // open: gt, lt
  // Probe on add_63_s
  Comparator #(.Bits(7)) comparator_63 (.a(add_63_s), .b(R), .eq(comparator_63_eq));  // open: gt, lt
  // Probe on add_64_s
  Comparator #(.Bits(7)) comparator_64 (.a(add_64_s), .b(R), .eq(comparator_64_eq));  // open: gt, lt
  assign driver_59_out = comparator_57_eq ? block4___solve_57_out : 64'bz;  // Driver driver_59
  Register #(.Bits(64)) register_57 (.D(driver_59_out), .C(C), .en(comparator_57_eq), .Q(out_11));
  assign driver_60_out = comparator_58_eq ? block4___solve_58_out : 64'bz;  // Driver driver_60
  Register #(.Bits(64)) register_58 (.D(driver_60_out), .C(C), .en(comparator_58_eq), .Q(out_19));
  assign driver_61_out = comparator_59_eq ? block4___solve_59_out : 64'bz;  // Driver driver_61
  Register #(.Bits(64)) register_59 (.D(driver_61_out), .C(C), .en(comparator_59_eq), .Q(out_27));
  assign driver_62_out = comparator_60_eq ? block4___solve_60_out : 64'bz;  // Driver driver_62
  Register #(.Bits(64)) register_60 (.D(driver_62_out), .C(C), .en(comparator_60_eq), .Q(out_35));
  assign driver_63_out = comparator_61_eq ? block4___solve_61_out : 64'bz;  // Driver driver_63
  Register #(.Bits(64)) register_61 (.D(driver_63_out), .C(C), .en(comparator_61_eq), .Q(out_43));
  assign driver_64_out = comparator_62_eq ? block4___solve_62_out : 64'bz;  // Driver driver_64
  Register #(.Bits(64)) register_62 (.D(driver_64_out), .C(C), .en(comparator_62_eq), .Q(out_51));
  assign driver_65_out = comparator_63_eq ? block4___solve_63_out : 64'bz;  // Driver driver_65
  Register #(.Bits(64)) register_63 (.D(driver_65_out), .C(C), .en(comparator_63_eq), .Q(out_59));
  assign driver_66_out = comparator_64_eq ? block4___solve_64_out : 64'bz;  // Driver driver_66
  Register #(.Bits(64)) register_64 (.D(driver_66_out), .C(C), .en(comparator_64_eq), .Q(out_67));

  // Notes on the sheet:
  //   Clock: Hz: 1000
  //   Ready: Hz: 2
  //   Enc_r: default 3496211750505947571
  //   Put the encrypted block into Enc_r to reverse it
endmodule
